# Fritzing sketch wiring-diagram (saved by Fritzing 0.9.4)
breadboards: 1

parts:
  Mod1 = Arduino MKR Wifi 1010
  R1 = Resistor [tolerance=±5% resistance=220 package="2010 [SMD]"]
  R2 = Resistor [tolerance=±5% resistance=220 package="2010 [SMD]"]
  R3 = Resistor [tolerance=±5% resistance=220 package="2010 [SMD]"]
  LED1 = RGB LED (com. cathode, rbg) [package="5 mm [THT]"]
  U1 = Liquid Level Sensor-FS-IR02 SKU SEN0205
  U2 = Liquid Level Sensor-FS-IR02 SKU SEN0205

nets:
  GND: Mod1.GND, LED1.common_cathode, U1.GND, U2.GND
  N1: Mod1.~D3, R1.Pin_1
  N2: Mod1.~D4, R2.Pin_1
  N3: Mod1.~D5, R3.Pin_1
  N4: Mod1.D7, U1.OUT
  N5: Mod1.D8/MOSI, U2.OUT
  VCC: Mod1.+5V, U1.VCC, U2.VCC
  N6: R1.Pin_0, LED1.red_anode
  N7: R2.Pin_0, LED1.green_anode
  N8: R3.Pin_0, LED1.blue_anode

custom parts:
  Arduino MKR Wifi 1010: Arduino MKR Wifi 1010, SAMD21 Cortex-M0+ 32bit Low Power ARM MCU,Flash Memory 256 KB, SRAM 32KB, 48mhz clock, Ublok Wifi interface.
  Liquid Level Sensor-FS-IR02 SKU SEN0205: This is a photoelectric liquid level sensor that is operates using traditional optical principles. The advantages of this are a high sensitivity and no need for mechanical parts - meaning less calibration! The corrosion resistant probe is easily mounted and can handle high temperatures and high pressures. The sensor is equipped with an interface adapter for compatibility with the DFRobot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
